// Digital circuit 1-bit-2-to-1-multiplexer.dig as structural Verilog
module _1_bit_2_to_1_multiplexer (
  input  A,
  input  S,
  input  B,
  output X
);

  wire and_1_out, and_2_out;

  and and_1 (and_1_out, A, ~S);  // And
  and and_2 (and_2_out, S, B);
  or or_1 (X, and_1_out, and_2_out);
endmodule
