// Digital circuit 4-bit-ripple-carry-adder.dig as structural Verilog
module _4_bit_ripple_carry_adder (
  input  [3:0] in_1,
  input  [3:0] in_3,
  output [3:0] out_2
);

  wire full_adder_1_c_out, full_adder_2_c_out, full_adder_3_c_out;

  full_adder full_adder_1 (.C_in(1'b0), .A(in_1[0]), .B(in_3[0]), .X(out_2[0]), .C_out(full_adder_1_c_out));
  full_adder full_adder_2 (
    .C_in(full_adder_1_c_out), .A(in_1[1]), .B(in_3[1]), .X(out_2[1]), .C_out(full_adder_2_c_out));
  full_adder full_adder_3 (
    .C_in(full_adder_2_c_out), .A(in_1[2]), .B(in_3[2]), .X(out_2[2]), .C_out(full_adder_3_c_out));
  full_adder full_adder_4 (.C_in(full_adder_3_c_out), .A(in_1[3]), .B(in_3[3]), .X(out_2[3]));  // open: C_out
endmodule
