// Digital circuit full-adder.dig as structural Verilog
module full_adder (
  input  C_in,
  input  A,
  input  B,
  output X,
  output C_out
);

  wire half_adder_1_c_out, half_adder_1_x, half_adder_2_c_out;

  half_adder half_adder_1 (.A(A), .B(B), .X(half_adder_1_x), .C_out(half_adder_1_c_out));
  half_adder half_adder_2 (.A(C_in), .B(half_adder_1_x), .X(X), .C_out(half_adder_2_c_out));
  or or_1 (C_out, half_adder_2_c_out, half_adder_1_c_out);
endmodule
