// Digital circuit alu.dig as structural Verilog
module alu (
  input  [15:0] A,
  input  [15:0] B,
  input  [1:0] Op,
  output [15:0] Result
);

  wire [15:0] add_1_s, and_1_out, not_1_out, or_1_out;

  Add #(.Bits(16)) add_1 (.a(A), .b(B), .c_i(1'b0), .s(add_1_s));  // open: c_o
  assign or_1_out = A | B;  // Or or_1, 16 bits wide
  assign and_1_out = A & B;  // And and_1, 16 bits wide
  assign not_1_out = ~A;  // Not not_1, 16 bits wide
  Multiplexer #(.Bits(16), .Selector_Bits(2)) multiplexer_1 (
    .sel(Op), .in_0(add_1_s), .in_1(or_1_out), .in_2(and_1_out), .in_3(not_1_out), .out(Result));
endmodule
