// Digital circuit d-flip-flop.dig as structural Verilog
module d_flip_flop (
  input  D,
  input  clk,
  output Q
);

  wire d_latch_1_q, not_1_out;

  d_latch d_latch_1 (.D(D), .en(not_1_out), .Q(d_latch_1_q));
  not not_1 (not_1_out, clk);
  d_latch d_latch_2 (.D(d_latch_1_q), .en(clk), .Q(Q));
endmodule
