// Digital circuit d-latch.dig as structural Verilog
module d_latch (
  input  D,
  input  en,
  output Q
);

  wire and_1_out, and_2_out;

  and and_1 (and_1_out, ~D, en);  // And
  and and_2 (and_2_out, D, en);
  sr_latch sr_latch_1 (.R(and_1_out), .S(and_2_out), .Q(Q));
endmodule
