// Digital circuit reg-file-partial.dig as structural Verilog
module reg_file_partial (
  input  Write_en,
  input  [2:0] Write_sel,
  input  [15:0] Write_data,
  input  clk
);

  wire demultiplexer_1_out_0, demultiplexer_1_out_1, demultiplexer_1_out_2, demultiplexer_1_out_3,
       demultiplexer_1_out_4, demultiplexer_1_out_5, demultiplexer_1_out_6, demultiplexer_1_out_7;
  wire [15:0] r0_q, r1_q, r2_q, r3_q, r4_q, r5_q, r6_q, r7_q;

  Demultiplexer #(.Selector_Bits(3)) demultiplexer_1 (
    .sel(Write_sel), .in(Write_en), .out_0(demultiplexer_1_out_0), .out_1(demultiplexer_1_out_1),
    .out_2(demultiplexer_1_out_2), .out_3(demultiplexer_1_out_3), .out_4(demultiplexer_1_out_4),
    .out_5(demultiplexer_1_out_5), .out_6(demultiplexer_1_out_6), .out_7(demultiplexer_1_out_7));
  Register #(.Bits(16)) r0 (.D(Write_data), .C(clk), .en(demultiplexer_1_out_0), .Q(r0_q));
  Register #(.Bits(16)) r1 (.D(Write_data), .C(clk), .en(demultiplexer_1_out_1), .Q(r1_q));
  Register #(.Bits(16)) r2 (.D(Write_data), .C(clk), .en(demultiplexer_1_out_2), .Q(r2_q));
  Register #(.Bits(16)) r3 (.D(Write_data), .C(clk), .en(demultiplexer_1_out_3), .Q(r3_q));
  Register #(.Bits(16)) r4 (.D(Write_data), .C(clk), .en(demultiplexer_1_out_4), .Q(r4_q));
  Register #(.Bits(16)) r5 (.D(Write_data), .C(clk), .en(demultiplexer_1_out_5), .Q(r5_q));
  Register #(.Bits(16)) r6 (.D(Write_data), .C(clk), .en(demultiplexer_1_out_6), .Q(r6_q));
  Register #(.Bits(16)) r7 (.D(Write_data), .C(clk), .en(demultiplexer_1_out_7), .Q(r7_q));
endmodule
