// Digital circuit cpu.dig as structural Verilog
module cpu (
  input  clk,
  input  [15:0] PC_data,
  input  PC_jump,
  input  RF_write_en,
  input  [2:0] RF_write_sel,
  input  [2:0] RF_read_sel_1,
  input  [2:0] RF_read_sel_2,
  input  [1:0] ALU_op,
  input  Mem_str,
  input  Output_sel
);

  wire [15:0] alu_1_result, multiplexer_1_out, pc_1_data_out, ramdualaccess_1_d1, ramdualaccess_1_d2,
       reg_file_1_read_data1, reg_file_1_read_data2;

  pc pc_1 (.clk(clk), .Data_in(PC_data), .ld(PC_jump), .Data_out(pc_1_data_out));
  reg_file reg_file_1 (
    .clk(clk), .Write_data(multiplexer_1_out), .Write_en(RF_write_en), .Write_sel(RF_write_sel),
    .Read_sel1(RF_read_sel_1), .Read_sel2(RF_read_sel_2), .Read_data1(reg_file_1_read_data1),
    .Read_data2(reg_file_1_read_data2));
  alu alu_1 (.A(reg_file_1_read_data1), .B(reg_file_1_read_data2), .Op(ALU_op), .Result(alu_1_result));
  RAMDualAccess #(.AddrBits(16), .Bits(16)) ramdualaccess_1 (
    .str(Mem_str), .C(clk), .ld(1'b1), .A1(reg_file_1_read_data1), .Din1(reg_file_1_read_data2),
    .A2(pc_1_data_out), .D1(ramdualaccess_1_d1), .D2(ramdualaccess_1_d2));
  Multiplexer #(.Bits(16)) multiplexer_1 (
    .sel(Output_sel), .in_0(alu_1_result), .in_1(ramdualaccess_1_d1), .out(multiplexer_1_out));
endmodule
