// Digital circuit pc.dig as structural Verilog
module pc (
  input  clk,
  input  [15:0] Data_in,
  input  ld,
  output [15:0] Data_out
);

  wire [15:0] add_1_s, multiplexer_1_out;

  Multiplexer #(.Bits(16)) multiplexer_1 (.sel(ld), .in_0(add_1_s), .in_1(Data_in), .out(multiplexer_1_out));
  D_FF #(.Bits(16)) d_ff_1 (.D(multiplexer_1_out), .C(clk), .Q(Data_out));  // open: nQ
  Add #(.Bits(16)) add_1 (.a(Data_out), .b(16'h1), .c_i(1'b0), .s(add_1_s));  // open: c_o
endmodule
