// Digital circuit reg-file.dig as structural Verilog
module reg_file (
  input  clk,
  input  [15:0] Write_data,
  input  Write_en,
  input  [2:0] Write_sel,
  input  [2:0] Read_sel1,
  input  [2:0] Read_sel2,
  output [15:0] Read_data1,
  output [15:0] Read_data2
);

  wire demultiplexer_1_out_1, demultiplexer_1_out_2, demultiplexer_1_out_3, demultiplexer_1_out_4,
       demultiplexer_1_out_5, demultiplexer_1_out_6, demultiplexer_1_out_7;
  wire [15:0] r1_q, r2_q, r3_q, r4_q, r5_q, r6_q, r7_q;

  Demultiplexer #(.Selector_Bits(3)) demultiplexer_1 (
    .sel(Write_sel), .in(Write_en), .out_1(demultiplexer_1_out_1), .out_2(demultiplexer_1_out_2),
    .out_3(demultiplexer_1_out_3), .out_4(demultiplexer_1_out_4), .out_5(demultiplexer_1_out_5),
    .out_6(demultiplexer_1_out_6), .out_7(demultiplexer_1_out_7));  // open: out_0
  Register #(.Bits(16)) r1 (.D(Write_data), .C(clk), .en(demultiplexer_1_out_1), .Q(r1_q));
  Register #(.Bits(16)) r2 (.D(Write_data), .C(clk), .en(demultiplexer_1_out_2), .Q(r2_q));
  Register #(.Bits(16)) r3 (.D(Write_data), .C(clk), .en(demultiplexer_1_out_3), .Q(r3_q));
  Register #(.Bits(16)) r4 (.D(Write_data), .C(clk), .en(demultiplexer_1_out_4), .Q(r4_q));
  Register #(.Bits(16)) r5 (.D(Write_data), .C(clk), .en(demultiplexer_1_out_5), .Q(r5_q));
  Register #(.Bits(16)) r6 (.D(Write_data), .C(clk), .en(demultiplexer_1_out_6), .Q(r6_q));
  Register #(.Bits(16)) r7 (.D(Write_data), .C(clk), .en(demultiplexer_1_out_7), .Q(r7_q));
  Multiplexer #(.Selector_Bits(3), .Bits(16)) multiplexer_1 (
    .sel(Read_sel1), .in_0({16{1'b0}}), .in_1(r1_q), .in_2(r2_q), .in_3(r3_q), .in_4(r4_q), .in_5(r5_q),
    .in_6(r6_q), .in_7(r7_q), .out(Read_data1));
  Multiplexer #(.Selector_Bits(3), .Bits(16)) multiplexer_2 (
    .sel(Read_sel2), .in_0({16{1'b0}}), .in_1(r1_q), .in_2(r2_q), .in_3(r3_q), .in_4(r4_q), .in_5(r5_q),
    .in_6(r6_q), .in_7(r7_q), .out(Read_data2));
endmodule
