// Digital circuit alu.dig as structural Verilog
module alu (
  input  [15:0] A,
  input  [15:0] B,
  input  [2:0] OP,
  output [15:0] Result,
  output [3:0] Flags
);

  wire xnor_1_out, xor_1_out;
  wire [15:0] add_1_s, and_1_out, multiplexer_1_out, not_1_out, not_2_out, notconnected_1_out,
       notconnected_2_out, notconnected_3_out, or_1_out;

  assign not_1_out = ~B;  // Not not_1, 16 bits wide
  Multiplexer #(.Bits(16)) multiplexer_1 (.sel(OP[2]), .in_0(B), .in_1(not_1_out), .out(multiplexer_1_out));
  Add #(.Bits(16)) add_1 (.a(A), .b(multiplexer_1_out), .c_i(OP[2]), .s(add_1_s), .c_o(Flags[2]));
  assign or_1_out = A | B;  // Or or_1, 16 bits wide
  assign and_1_out = A & B;  // And and_1, 16 bits wide
  assign not_2_out = ~A;  // Not not_2, 16 bits wide
  // NotConnected on notconnected_1_out
  // NotConnected on notconnected_2_out
  // NotConnected on notconnected_3_out
  Multiplexer #(.Selector_Bits(3), .Bits(16)) multiplexer_2 (
    .sel(OP), .in_0(add_1_s), .in_1(or_1_out), .in_2(and_1_out), .in_3(not_2_out), .in_4(add_1_s),
    .in_5(notconnected_1_out), .in_6(notconnected_2_out), .in_7(notconnected_3_out),
    .out({Flags[1], Result[14:0]}));
  xnor xnor_1 (xnor_1_out, A[15], multiplexer_1_out[15]);
  xor xor_1 (xor_1_out, multiplexer_1_out[15], Flags[1]);
  Comparator #(.Bits(16)) comparator_1 (.a({16{1'b0}}), .b({Flags[1], Result[14:0]}), .eq(Flags[0]));  // open: gt, lt
  and and_2 (Flags[3], xnor_1_out, xor_1_out);

  assign Result[15] = Flags[1];
endmodule

/* Test case ops:
	A B OP Result
loop(i,1000)
 let a = random(1<<16);
 let b = random(1<<16);
	(a) (b) (0) ((a+b) & 0xFFFF)
	(a) (b) (1) ((a|b) & 0xFFFF)
	(a) (b) (2) ((a&b) & 0xFFFF)
	(a) (b) (3) ((~a ) & 0xFFFF)
	(a) (b) (4) ((a-b) & 0xFFFF)
end loop
*/

/* Test case Z:
	A B OP Z
declare Z = Flags & 1;

0 0 3 0
0xFFFF 0 3 ((~0xFFFF & 0xFFFF) = 0)

loop(i,10)
 let a = random(1<<16);
	(a) (-a) 0 1
	(a) (a) 4 1
end loop

loop(i,100000)
 let a = random(1<<16);
 let b = random(1<<16);
	(a) (b) (0) (((a+b) & 0xFFFF) = 0)
	(a) (b) (1) ((a|b) = 0)
	(a) (b) (2) ((a&b) = 0)
	(a) (b) (3) ((~a & 0xFFFF) = 0)
	(a) (b) (4) (((a-b) & 0xFFFF) = 0)
end loop
*/
