// Digital circuit and-transistors.dig as structural Verilog
module and_transistors (
  input  in_1,
  input  in_2,
  input  in_4,
  input  in_5,
  output out_3,
  output out_6
);

  wire nfet_1_s, nfet_3_s;

  NFET nfet_1 (.G(in_1), .D(1'b1), .S(nfet_1_s));
  NFET nfet_2 (.G(in_2), .D(nfet_1_s), .S(out_3));
  PullDown pulldown_1 (.out(out_3));
  NFET nfet_3 (.G(in_4), .D(1'b1), .S(nfet_3_s));
  NFET nfet_4 (.G(in_5), .D(nfet_3_s), .S(out_6));
  PFET pfet_1 (.G(in_4), .S(out_6), .D(1'b0));
  PFET pfet_2 (.G(in_5), .S(out_6), .D(1'b0));

  // Notes on the sheet:
  //   Resistor-Transistor-Logic
  //   AND gates
  //   Transistor-Transistor-Logic
endmodule
