// Digital circuit condition_checker.dig as structural Verilog
module condition_checker (
  input  [3:0] Flags,
  input  [3:0] JumpCode,
  output Jump
);

  wire and_1_out, and_2_out, decoder_1_out_0, decoder_1_out_1, decoder_1_out_15;

  Decoder #(.Selector_Bits(4)) decoder_1 (
    .sel(JumpCode), .out_0(decoder_1_out_0), .out_1(decoder_1_out_1), .out_15(decoder_1_out_15));  // open: out_2, out_3, out_4, out_5, out_6, out_7, out_8, out_9, out_10, out_11, out_12, out_13, out_14
  and and_1 (and_1_out, decoder_1_out_0, ~Flags[0]);  // And
  and and_2 (and_2_out, decoder_1_out_1, Flags[0]);
  or or_1 (Jump, and_1_out, and_2_out, 1'b0, 1'b0, 1'b0, 1'b0, 1'b0, 1'b0, 1'b0, 1'b0, 1'b0, 1'b0, 1'b0, 1'b0, 1'b0, decoder_1_out_15);
endmodule
