// Digital circuit control_unit.dig as structural Verilog
module control_unit (
  input  [15:0] Instr,
  input  [3:0] Flags,
  output [2:0] RF_ws,
  output [2:0] RF_rs1,
  output [2:0] RF_rs2,
  output Mem_str,
  output RF_we,
  output PC_jump,
  output [15:0] PC_data,
  output [2:0] ALU_op,
  output ALU_z,
  output [15:0] Output_imm,
  output [1:0] Output_sel,
  output PC_load,
  output PC_src,
  output ALU_n,
  output ALU_c,
  output ALU_v
);

  wire and_1_out, and_2_out, and_4_out, and_5_out, and_6_out, and_8_out, condition_checker_1_jump, nor_1_out;
  wire [15:0] bitextender_1_out, bitextender_2_out;

  and and_1 (and_1_out, ~Instr[15], Instr[14]);  // And
  and and_2 (and_2_out, ~Instr[15], Instr[12]);  // And
  condition_checker condition_checker_1 (.Flags(Flags), .JumpCode(Instr[11:8]), .Jump(condition_checker_1_jump));
  nor nor_1 (nor_1_out, Instr[0], Instr[1], Instr[2], Instr[3], Instr[4], Instr[5], Instr[7], Instr[8], Instr[9], Instr[10], Instr[11], Instr[6]);
  or or_1 (Output_sel[0], and_1_out, and_2_out);
  nor nor_2 (Output_sel[1], Instr[14], Instr[15]);
  BitExtender bitextender_1 (.in(Instr[7:0]), .out(bitextender_1_out));
  BitExtender #(.inputBits(12)) bitextender_2 (.in(Instr[11:0]), .out(bitextender_2_out));
  Multiplexer #(.Bits(3)) multiplexer_1 (.sel(Mem_str), .in_0(Instr[2:0]), .in_1(Instr[10:8]), .out(RF_rs2));
  and and_3 (Mem_str, Instr[12], ~Instr[13], Instr[14], ~Instr[15]);  // And
  and and_4 (and_4_out, ~Instr[12], Instr[13], ~Instr[14], ~Instr[15]);  // And
  and and_5 (and_5_out, Instr[12], Instr[13], ~Instr[14], ~Instr[15]);  // And
  Multiplexer #(.Bits(16)) multiplexer_2 (
    .sel(Instr[12]), .in_0(bitextender_1_out), .in_1(bitextender_2_out), .out(PC_data));
  and and_6 (and_6_out, and_4_out, condition_checker_1_jump);
  and and_7 (ALU_c, Instr[15], ~Instr[13], ~Instr[12]);  // And
  and and_8 (and_8_out, and_5_out, ~nor_1_out);  // And
  and and_9 (PC_load, and_5_out, nor_1_out);
  Multiplexer #(.Bits(3)) multiplexer_3 (.sel(PC_load), .in_0(Instr[6:4]), .in_1(3'b111), .out(RF_rs1));
  Multiplexer #(.Bits(3)) multiplexer_4 (.sel(and_8_out), .in_0(Instr[10:8]), .in_1(3'b111), .out(RF_ws));
  nor nor_3 (RF_we, Mem_str, PC_load, and_4_out);
  or or_2 (PC_jump, and_6_out, and_8_out);

  assign ALU_n = Instr[15];
  assign ALU_op = Instr[14:12];
  assign ALU_v = ALU_c;
  assign ALU_z = Instr[15];
  assign Output_imm = {{8{1'b0}}, Instr[7:0]};
  assign PC_src = PC_load;
endmodule

/* Test case put:
	Instr   Flags ALU_op Output_imm PC_data RF_rs1 RF_rs2 RF_ws RF_we Mem_str PC_jump PC_load PC_src ALU_z Output_sel

loop(r,8)
 let instr = 0x0009 | (r << 8);
	(instr) X X      0x9        X       X      X      (r)   1     0       0       0       X      0     2
end loop
*/

/* Test case j:
	Instr   Flags ALU_op Output_imm PC_data            RF_rs1 RF_rs2 RF_ws RF_we Mem_str PC_jump PC_load PC_src ALU_z Output_sel

loop(n,2)
  let a = random(1<<8);
  let instr = 0x2000 | a;
	(instr | 0 << 8) 00 X      X          (signExt(8,a))    X      X      X     0     0        1      0      0      0     X
	(instr | 0 << 8) 01 X      X          X                 X      X      X     0     0        0      0      0      0     X

	(instr | 1 << 8) 00 X      X          (signExt(8,a))    X      X      X     0     0        0      0      0      0     X
	(instr | 1 << 8) 01 X      X          X                 X      X      X     0     0        1      0      0      0     X

end loop
*/

/* Test case call:
	Instr   Flags ALU_op Output_imm PC_data          RF_rs1 RF_rs2 RF_ws RF_we Mem_str PC_jump PC_load PC_src ALU_z Output_sel

loop(n, 100)
 let a = random((1<<12)-1) + 1;
 let instr = 0x3000 | a;
	(instr) X X      X          (signExt(12,a))  X      X      0x7   1     0       1       0       0      0     3
end loop
	0x3000  X X      X          X                0x7    X      X     0     0       0       1       1      0     X
*/

/* Test case ldr/str:
	Instr   Flags ALU_op Output_imm PC_data RF_rs1 RF_rs2 RF_ws RF_we Mem_str PC_jump PC_load PC_src ALU_z Output_sel

loop(rd,8)
 loop(ra,8)
  let ldr = 0x4000 | rd << 8 | ra << 4;
  let str = 0x5000 | rd << 8 | ra << 4;
        (ldr) X X X X (ra) X    (rd) 1 0 0 0 X 0 1
	(str) X X X X (ra) (rd) X    0 1 0 0 X 0 X
 end loop
end loop
*/

/* Test case alu:
	Instr   Flags ALU_op Output_imm PC_data RF_rs1 RF_rs2 RF_ws RF_we Mem_str PC_jump PC_load PC_src ALU_z Output_sel

loop(d,2)
 let rd = random(8);
 loop(a,2)
  let ra = random(8);
  loop(b,2)
   let rb = random(8);

	(0x8000 | rd << 8 | ra << 4 | rb) X 0 X X (ra) (rb) (rd) 1 0 0 0 X 1 0
	(0x9000 | rd << 8 | ra << 4 | rb) X 1 X X (ra) (rb) (rd) 1 0 0 0 X 1 0
	(0xA000 | rd << 8 | ra << 4 | rb) X 2 X X (ra) (rb) (rd) 1 0 0 0 X 1 0
	(0xC000 | rd << 8 | ra << 4 | rb) X 4 X X (ra) (rb) (rd) 1 0 0 0 X 1 0
	
  end loop
    
	(0xB000 | rd << 8 | ra << 4) X 3 X X (ra) X (rd) 1 0 0 0 X 1 0

 end loop
end loop
*/
