// Digital circuit cpu.dig as structural Verilog
module cpu (
  input  clk
);

  wire alu_1_p5, control_unit_1_alu_c, control_unit_1_alu_n, control_unit_1_alu_v, control_unit_1_alu_z,
       control_unit_1_mem_str, control_unit_1_pc_jump, control_unit_1_pc_load, control_unit_1_pc_src,
       control_unit_1_rf_we;
  wire [1:0] control_unit_1_output_sel;
  wire [2:0] control_unit_1_alu_op, control_unit_1_rf_rs1, control_unit_1_rf_rs2, control_unit_1_rf_ws;
  wire [3:0] flags_reg_1_p7;
  wire [15:0] alu_1_p4, control_unit_1_output_imm, control_unit_1_pc_data, multiplexer_1_out,
       multiplexer_2_out, pc_1_x, pc_1_x_next, ramdualaccess_1_d1, ramdualaccess_1_d2, reg_file_1_read1_out,
       reg_file_1_read2_out;

  control_unit control_unit_1 (
    .Instr(ramdualaccess_1_d2), .Flags(flags_reg_1_p7), .RF_ws(control_unit_1_rf_ws),
    .RF_rs1(control_unit_1_rf_rs1), .RF_rs2(control_unit_1_rf_rs2), .Mem_str(control_unit_1_mem_str),
    .RF_we(control_unit_1_rf_we), .PC_jump(control_unit_1_pc_jump), .PC_data(control_unit_1_pc_data),
    .ALU_op(control_unit_1_alu_op), .ALU_z(control_unit_1_alu_z), .Output_imm(control_unit_1_output_imm),
    .Output_sel(control_unit_1_output_sel), .PC_load(control_unit_1_pc_load), .PC_src(control_unit_1_pc_src),
    .ALU_n(control_unit_1_alu_n), .ALU_c(control_unit_1_alu_c), .ALU_v(control_unit_1_alu_v));
  Multiplexer #(.Bits(16)) multiplexer_1 (
    .sel(control_unit_1_pc_src), .in_0(control_unit_1_pc_data), .in_1(reg_file_1_read1_out),
    .out(multiplexer_1_out));
  pc pc_1 (
    .clk(clk), .offset(control_unit_1_pc_jump), .D(multiplexer_1_out), .load(control_unit_1_pc_load),
    .X(pc_1_x), .X_next(pc_1_x_next));
  reg_file reg_file_1 (
    .clk(clk), .Write_data(multiplexer_2_out), .Write_en(control_unit_1_rf_we),
    .Write_sel(control_unit_1_rf_ws), .Read1_sel(control_unit_1_rf_rs1), .Read2_sel(control_unit_1_rf_rs2),
    .Read1_out(reg_file_1_read1_out), .Read2_out(reg_file_1_read2_out));
  // alu alu_1: pin names not known; wires that end beside it: reg_file_1_read1_out, reg_file_1_read2_out, control_unit_1_alu_op, alu_1_p4, alu_1_p5
  RAMDualAccess #(.AddrBits(16), .isProgramMemory("true"), .Bits(16)) ramdualaccess_1 (
    .str(control_unit_1_mem_str), .C(clk), .ld(1'b1), .A1(reg_file_1_read1_out), .Din1(reg_file_1_read2_out),
    .A2(pc_1_x), .D1(ramdualaccess_1_d1), .D2(ramdualaccess_1_d2));
  // flags_reg flags_reg_1: pin names not known; wires that end beside it: clk, alu_1_p5, control_unit_1_alu_z, control_unit_1_alu_n, control_unit_1_alu_c, control_unit_1_alu_v, flags_reg_1_p7
  Multiplexer #(.Selector_Bits(2), .Bits(16)) multiplexer_2 (
    .sel(control_unit_1_output_sel), .in_0(alu_1_p4), .in_1(ramdualaccess_1_d1),
    .in_2(control_unit_1_output_imm), .in_3(pc_1_x_next), .out(multiplexer_2_out));
  // Probe Flags on flags_reg_1_p7
  // Probe Instruction on ramdualaccess_1_d2
endmodule
