// Digital circuit d-flipflop-transistors.dig as structural Verilog
module d_flipflop_transistors (
  input  en,
  input  D,
  input  clk,
  input  en_2,
  input  D_2,
  input  clk_2,
  output out,
  output out_2
);

  wire nfet_1_d, nfet_2_s, nfet_3_s, nfet_4_s, nfet_5_s, nfet_6_s, nfet_8_d, nfet_9_d, nfet_10_s, nfet_11_s,
       nfet_12_s, nfet_13_s, nfet_15_s, nfet_16_s, nfet_17_s, nfet_18_s, nfet_19_d, nfet_21_d, nfet_23_s,
       nfet_24_d, nfet_26_d, nfet_29_s, nfet_30_s, nfet_31_s, nfet_32_s, nfet_33_s, nfet_34_s, nfet_35_s,
       nfet_38_d, pfet_1_d, pfet_2_d, pfet_3_d, pfet_4_d, pfet_5_d, pullup_8_out, pullup_10_out;

  NFET nfet_1 (.G(en), .D(nfet_1_d), .S(1'b0));
  NFET nfet_2 (.G(out), .D(1'b1), .S(nfet_2_s));
  NFET nfet_3 (.G(nfet_1_d), .D(nfet_2_s), .S(nfet_3_s));
  PullUp pullup_1 (.out(nfet_1_d));
  NFET nfet_4 (.G(en), .D(1'b1), .S(nfet_4_s));
  NFET nfet_5 (.G(D), .D(nfet_4_s), .S(nfet_5_s));
  PullDown pulldown_1 (.out(nfet_3_s));
  PullDown pulldown_2 (.out(nfet_5_s));
  NFET nfet_6 (.G(nfet_3_s), .D(1'b1), .S(nfet_6_s));
  NFET nfet_7 (.G(nfet_5_s), .D(1'b1), .S(nfet_6_s));
  PullDown pulldown_3 (.out(nfet_6_s));
  NFET nfet_8 (.G(nfet_6_s), .D(nfet_8_d), .S(1'b0));
  NFET nfet_9 (.G(clk), .D(nfet_9_d), .S(1'b0));
  NFET nfet_10 (.G(out_2), .D(1'b1), .S(nfet_10_s));
  PFET pfet_1 (.G(en_2), .S(nfet_10_s), .D(pfet_1_d));
  PullDown pulldown_4 (.out(pfet_1_d));
  NFET nfet_11 (.G(en_2), .D(1'b1), .S(nfet_11_s));
  NFET nfet_12 (.G(D_2), .D(nfet_11_s), .S(nfet_12_s));
  PullDown pulldown_5 (.out(nfet_12_s));
  PullUp pullup_2 (.out(nfet_8_d));
  PullUp pullup_3 (.out(nfet_9_d));
  NFET nfet_13 (.G(pfet_1_d), .D(1'b1), .S(nfet_13_s));
  NFET nfet_14 (.G(nfet_12_s), .D(1'b1), .S(nfet_13_s));
  PullDown pulldown_6 (.out(nfet_13_s));
  NFET nfet_15 (.G(nfet_8_d), .D(1'b1), .S(nfet_15_s));
  NFET nfet_16 (.G(nfet_9_d), .D(nfet_15_s), .S(nfet_16_s));
  PullDown pulldown_7 (.out(nfet_16_s));
  NFET nfet_17 (.G(nfet_6_s), .D(1'b1), .S(nfet_17_s));
  NFET nfet_18 (.G(nfet_9_d), .D(nfet_17_s), .S(nfet_18_s));
  PullDown pulldown_8 (.out(nfet_18_s));
  NFET nfet_19 (.G(nfet_21_d), .D(nfet_19_d), .S(1'b0));
  NFET nfet_20 (.G(nfet_16_s), .D(nfet_19_d), .S(1'b0));
  NFET nfet_21 (.G(nfet_19_d), .D(nfet_21_d), .S(1'b0));
  NFET nfet_22 (.G(nfet_18_s), .D(nfet_21_d), .S(1'b0));
  PFET pfet_2 (.G(nfet_13_s), .S(1'b1), .D(pfet_2_d));
  PFET pfet_3 (.G(clk_2), .S(pfet_2_d), .D(pfet_3_d));
  PullDown pulldown_9 (.out(pfet_3_d));
  NFET nfet_23 (.G(nfet_13_s), .D(1'b1), .S(nfet_23_s));
  PFET pfet_4 (.G(clk_2), .S(nfet_23_s), .D(pfet_4_d));
  PullDown pulldown_10 (.out(pfet_4_d));
  PullUp pullup_4 (.out(nfet_19_d));
  PullUp pullup_5 (.out(nfet_21_d));
  NFET nfet_24 (.G(nfet_26_d), .D(nfet_24_d), .S(1'b0));
  NFET nfet_25 (.G(pfet_3_d), .D(nfet_24_d), .S(1'b0));
  NFET nfet_26 (.G(nfet_24_d), .D(nfet_26_d), .S(1'b0));
  NFET nfet_27 (.G(pfet_4_d), .D(nfet_26_d), .S(1'b0));
  PullUp pullup_6 (.out(nfet_24_d));
  PullUp pullup_7 (.out(nfet_26_d));
  PullUp pullup_8 (.out(pullup_8_out));
  NFET nfet_28 (.G(nfet_19_d), .D(pullup_8_out), .S(1'b0));
  NFET nfet_29 (.G(pullup_8_out), .D(1'b1), .S(nfet_29_s));
  NFET nfet_30 (.G(clk), .D(nfet_29_s), .S(nfet_30_s));
  NFET nfet_31 (.G(nfet_19_d), .D(1'b1), .S(nfet_31_s));
  NFET nfet_32 (.G(clk), .D(nfet_31_s), .S(nfet_32_s));
  PFET pfet_5 (.G(nfet_24_d), .S(1'b1), .D(pfet_5_d));
  NFET nfet_33 (.G(clk_2), .D(pfet_5_d), .S(nfet_33_s));
  NFET nfet_34 (.G(nfet_24_d), .D(1'b1), .S(nfet_34_s));
  NFET nfet_35 (.G(clk_2), .D(nfet_34_s), .S(nfet_35_s));
  PullDown pulldown_11 (.out(nfet_30_s));
  PullDown pulldown_12 (.out(nfet_32_s));
  PullDown pulldown_13 (.out(nfet_33_s));
  PullDown pulldown_14 (.out(nfet_35_s));
  NFET nfet_36 (.G(nfet_38_d), .D(out), .S(1'b0));
  NFET nfet_37 (.G(nfet_30_s), .D(out), .S(1'b0));
  NFET nfet_38 (.G(out), .D(nfet_38_d), .S(1'b0));
  NFET nfet_39 (.G(nfet_32_s), .D(nfet_38_d), .S(1'b0));
  PullUp pullup_9 (.out(out_2));
  NFET nfet_40 (.G(pullup_10_out), .D(out_2), .S(1'b0));
  NFET nfet_41 (.G(nfet_33_s), .D(out_2), .S(1'b0));
  PullUp pullup_10 (.out(pullup_10_out));
  NFET nfet_42 (.G(out_2), .D(pullup_10_out), .S(1'b0));
  NFET nfet_43 (.G(nfet_35_s), .D(pullup_10_out), .S(1'b0));
  PullUp pullup_11 (.out(out));
  PullUp pullup_12 (.out(nfet_38_d));
endmodule
