// Digital circuit flags_reg.dig as structural Verilog
module flags_reg (
  input  clk,
  input  [3:0] Flags_in,
  input  Write_Z,
  input  Write_N,
  input  Write_C,
  input  Write_V,
  output [3:0] Flags_out
);

  Register register_1 (.D(Flags_in[0]), .C(clk), .en(Write_Z), .Q(Flags_out[0]));
  Register register_2 (.D(Flags_in[1]), .C(clk), .en(Write_N), .Q(Flags_out[1]));
  Register register_3 (.D(Flags_in[2]), .C(clk), .en(Write_C), .Q(Flags_out[2]));
  Register register_4 (.D(Flags_in[3]), .C(clk), .en(Write_V), .Q(Flags_out[3]));
  // Pins of 1 and 4 bits meet at Flags_in
endmodule
