// Digital circuit full-adder-transistors.dig as structural Verilog
module full_adder_transistors (
  input  A,
  input  B,
  input  C_in,
  output S,
  output C_out
);

  wire nfet_1_s, nfet_3_d, nfet_3_s, nfet_5_d, nfet_5_s, nfet_7_d, nfet_9_d, nfet_11_d, nfet_11_s, nfet_13_d,
       nfet_13_s, nfet_15_d, nfet_17_d, pullup_1_out, pullup_4_out, pullup_5_out;

  PullUp pullup_1 (.out(pullup_1_out));
  NFET nfet_1 (.G(A), .D(pullup_1_out), .S(nfet_1_s));
  NFET nfet_2 (.G(B), .D(nfet_1_s), .S(1'b0));
  NFET nfet_3 (.G(A), .D(nfet_3_d), .S(nfet_3_s));
  NFET nfet_4 (.G(pullup_1_out), .D(nfet_3_d), .S(1'b0));
  NFET nfet_5 (.G(pullup_1_out), .D(nfet_5_d), .S(nfet_5_s));
  NFET nfet_6 (.G(B), .D(nfet_5_s), .S(1'b0));
  PullUp pullup_2 (.out(nfet_3_s));
  PullUp pullup_3 (.out(nfet_5_d));
  PullUp pullup_4 (.out(pullup_4_out));
  NFET nfet_7 (.G(nfet_3_s), .D(nfet_7_d), .S(pullup_4_out));
  NFET nfet_8 (.G(nfet_5_d), .D(nfet_7_d), .S(1'b0));
  PullUp pullup_5 (.out(pullup_5_out));
  NFET nfet_9 (.G(pullup_4_out), .D(nfet_9_d), .S(pullup_5_out));
  NFET nfet_10 (.G(C_in), .D(nfet_9_d), .S(1'b0));
  NFET nfet_11 (.G(pullup_4_out), .D(nfet_11_d), .S(nfet_11_s));
  NFET nfet_12 (.G(pullup_5_out), .D(nfet_11_d), .S(1'b0));
  NFET nfet_13 (.G(pullup_5_out), .D(nfet_13_d), .S(nfet_13_s));
  NFET nfet_14 (.G(C_in), .D(nfet_13_d), .S(1'b0));
  PullUp pullup_6 (.out(nfet_11_s));
  PullUp pullup_7 (.out(nfet_13_s));
  PullUp pullup_8 (.out(S));
  NFET nfet_15 (.G(nfet_11_s), .D(nfet_15_d), .S(S));
  NFET nfet_16 (.G(nfet_13_s), .D(nfet_15_d), .S(1'b0));
  PullUp pullup_9 (.out(C_out));
  NFET nfet_17 (.G(pullup_5_out), .D(nfet_17_d), .S(C_out));
  NFET nfet_18 (.G(pullup_1_out), .D(nfet_17_d), .S(1'b0));
endmodule
