// Digital circuit pc.dig as structural Verilog
module pc (
  input  clk,
  input  offset,
  input  [15:0] D,
  input  load,
  output [15:0] X,
  output [15:0] X_next
);

  wire [15:0] add_1_s, multiplexer_1_out, multiplexer_2_out;

  Multiplexer #(.Bits(16)) multiplexer_1 (.sel(load), .in_0(add_1_s), .in_1(D), .out(multiplexer_1_out));
  Multiplexer #(.Bits(16)) multiplexer_2 (.sel(offset), .in_0(16'h1), .in_1(D), .out(multiplexer_2_out));
  Register #(.Bits(16)) PC (.D(multiplexer_1_out), .C(clk), .en(1'b1), .Q(X));
  Add #(.Bits(16)) add_1 (.a(multiplexer_2_out), .b(X), .c_i(1'b0), .s(add_1_s));  // open: c_o
  Add #(.Bits(16)) add_2 (.a(16'h1), .b(X), .c_i(1'b0), .s(X_next));  // open: c_o
endmodule
